// Logisim project contador_assincrono.circ as structural Verilog: 1 circuit, main circuit main
module main (
  output [6:0] out_1
);

  wire and_1_out, clock_1_out;

  Clock clock_1 (.out(clock_1_out));
  J_K_Flip_Flop #(.trigger("falling")) j_k_ff_1 (
    .J(1'b1), .clk(clock_1_out), .K(1'b1), .Q(out_1[0]), .preset(and_1_out));  // open: Qn, en, reset
  and and_1 (and_1_out, out_1[1], out_1[3], out_1[6]);
  J_K_Flip_Flop #(.trigger("falling")) j_k_ff_2 (
    .J(1'b1), .clk(out_1[0]), .K(1'b1), .Q(out_1[1]), .preset(and_1_out));  // open: Qn, en, reset
  J_K_Flip_Flop #(.trigger("falling")) j_k_ff_3 (
    .J(1'b1), .clk(out_1[1]), .K(1'b1), .Q(out_1[2]), .reset(and_1_out));  // open: Qn, preset, en
  J_K_Flip_Flop #(.trigger("falling")) j_k_ff_4 (
    .J(1'b1), .clk(out_1[2]), .K(1'b1), .Q(out_1[3]), .reset(and_1_out));  // open: Qn, preset, en
  J_K_Flip_Flop #(.trigger("falling")) j_k_ff_5 (
    .J(1'b1), .clk(out_1[3]), .K(1'b1), .Q(out_1[4]), .reset(and_1_out));  // open: Qn, preset, en
  J_K_Flip_Flop #(.trigger("falling")) j_k_ff_6 (
    .J(1'b1), .clk(out_1[4]), .K(1'b1), .Q(out_1[5]), .reset(and_1_out));  // open: Qn, preset, en
  J_K_Flip_Flop #(.trigger("falling")) j_k_ff_7 (
    .J(1'b1), .clk(out_1[5]), .K(1'b1), .Q(out_1[6]), .reset(and_1_out));  // open: Qn, preset, en

  // Other names for the same wires on the sheet: A = out_1[1]; B = out_1[3]; C = out_1[6]

  // Notes on the sheet:
  //   Matrícula: 2024520249
  //   Q0
  //   0000011
  //   1001010
  //   Nome: Gabriel Lorenson Schirmer
  //   Q1
  //   1001001 73 em binário
  //   3 em binário
  //   Q3
  //   Q2
  //   Quando os 1's do numero 74 forem verdadeiros. A.B.C = 1, preseta os dois primeiros bits e reseta os outros. = 0000011 = 3
  //   Q4
  //   74 em binário (pois ele conta até o 73 e quando der 74 ele volta para o 3)
  //   Q5
  //   Q6
  //   x = 3     0000011
  //   y = 73   1001001
endmodule
