// Logisim project contador_sincrono.circ as structural Verilog: 1 circuit, main circuit main
module main (
);

  wire and_2_out, and_3_out, clock_1_out, JA, KA, KC, KD, not_1_out, not_2_out, not_3_out, nQC, QA, QB, QC,
       QD;

  Clock clock_1 (.out(clock_1_out));
  J_K_Flip_Flop #(.trigger("falling")) j_k_ff_1 (
    .J(JA), .clk(clock_1_out), .K(KA), .Q(QA));  // open: Qn, preset, en, reset
  and and_1 (KA, QB, QD);
  not not_1 (not_1_out, QA);
  not not_2 (not_2_out, QB);
  and and_2 (and_2_out, not_1_out, not_2_out);
  and and_3 (and_3_out, QB, QD, QA);
  J_K_Flip_Flop #(.trigger("falling")) j_k_ff_2 (
    .J(QC), .clk(clock_1_out), .K(QD), .Q(QB));  // open: Qn, preset, en, reset
  or or_1 (KC, and_2_out, and_3_out);
  not not_3 (not_3_out, QB);
  J_K_Flip_Flop #(.trigger("falling")) j_k_ff_3 (
    .J(nQC), .clk(clock_1_out), .K(KC), .Q(QC), .Qn(nQC));  // open: preset, en, reset
  and and_4 (KD, not_3_out, QC);
  // Probe on {QA, QB, QC, QD}
  and and_5 (JA, QB, QC);
  J_K_Flip_Flop #(.trigger("falling")) j_k_ff_4 (
    .J(QB), .clk(clock_1_out), .K(KD), .Q(QD));  // open: Qn, preset, en, reset

  // Notes on the sheet:
  //   Nome: Gabriel Lorenson Schirmer
  //   Matrícula: 2024520249
  //   Ordem utilizada
  //   1
  //   3
  //   4
  //   7
  //   11
  //   14
  //   15
endmodule
