// Logisim project cpfmatricula_display.circ as structural Verilog: 3 circuits, main circuit main
module main (
);

  wire clock_1_out, clock_2_out, codificador_cpf_1_a_2, codificador_cpf_1_b_2, codificador_cpf_1_c_2,
       codificador_cpf_1_d_2, codificador_cpf_1_e, codificador_cpf_1_f, codificador_cpf_1_g,
       codificador_cpf_1_ponto, codificador_matricula_1_a_2, codificador_matricula_1_b_2,
       codificador_matricula_1_c_2, codificador_matricula_1_d_2, codificador_matricula_1_e,
       codificador_matricula_1_f, codificador_matricula_1_g;
  wire [3:0] counter_1_q, counter_2_q;

  Counter #(.width(4), .max('hf)) counter_1 (
    .count(1'b1), .Q(counter_1_q), .clk(clock_1_out));  // open: load, D, carry, clr
  Clock clock_1 (.out(clock_1_out));
  Counter #(.width(4), .max('hf)) counter_2 (
    .count(1'b1), .Q(counter_2_q), .clk(clock_2_out));  // open: load, D, carry, clr
  Clock clock_2 (.out(clock_2_out));
  codificador_cpf codificador_cpf_1 (
    .A(counter_1_q[3]), .B(counter_1_q[2]), .C(counter_1_q[1]), .D(counter_1_q[0]),
    .a_2(codificador_cpf_1_a_2), .b_2(codificador_cpf_1_b_2), .c_2(codificador_cpf_1_c_2),
    .d_2(codificador_cpf_1_d_2), .e(codificador_cpf_1_e), .f(codificador_cpf_1_f), .g(codificador_cpf_1_g),
    .ponto(codificador_cpf_1_ponto));
  codificador_matricula codificador_matricula_1 (
    .A(counter_2_q[3]), .B(counter_2_q[2]), .C(counter_2_q[1]), .D(counter_2_q[0]),
    .a_2(codificador_matricula_1_a_2), .b_2(codificador_matricula_1_b_2), .c_2(codificador_matricula_1_c_2),
    .d_2(codificador_matricula_1_d_2), .e(codificador_matricula_1_e), .f(codificador_matricula_1_f),
    .g(codificador_matricula_1_g));
  _7_Segment_Display u_7_segment_display_1 (
    .g(codificador_cpf_1_g), .f(codificador_cpf_1_f), .a(codificador_cpf_1_a_2), .b(codificador_cpf_1_b_2),
    .e(codificador_cpf_1_e), .d(codificador_cpf_1_d_2), .c(codificador_cpf_1_c_2),
    .dp(codificador_cpf_1_ponto));
  _7_Segment_Display u_7_segment_display_2 (
    .g(codificador_matricula_1_g), .f(codificador_matricula_1_f), .a(codificador_matricula_1_a_2),
    .b(codificador_matricula_1_b_2), .e(codificador_matricula_1_e), .d(codificador_matricula_1_d_2),
    .c(codificador_matricula_1_c_2));  // open: dp

  // Notes on the sheet:
  //   Matrícula: 2024520249
  //   Nome: Gabriel Lorenson Schirmer
  //   Matrícula: 2024520249
  //   CPF: 032.876.010-24
endmodule

module codificador_cpf (
  input  A,
  input  B,
  input  C,
  input  D,
  output a_2,
  output b_2,
  output c_2,
  output d_2,
  output e,
  output f,
  output g,
  output ponto
);

  wire and_1_out, and_2_out, and_3_out, and_4_out, and_5_out, and_6_out, and_7_out, and_8_out, and_9_out,
       and_10_out, and_11_out, and_12_out, and_13_out, and_14_out, and_15_out, and_16_out, and_17_out,
       and_18_out, and_19_out, and_20_out, and_21_out, and_22_out, and_23_out, and_24_out, and_25_out,
       and_26_out, and_27_out, and_28_out, and_29_out, and_30_out, not_1_out, not_2_out, not_3_out,
       not_4_out, not_5_out, not_6_out, not_7_out, not_8_out, not_9_out, not_10_out, not_11_out, not_12_out,
       not_13_out, not_14_out, not_15_out, not_16_out, not_17_out, not_18_out, not_19_out, not_20_out,
       not_21_out, not_22_out, not_23_out, not_24_out, not_25_out, not_26_out, not_27_out, not_28_out,
       not_29_out, not_30_out, not_31_out, not_32_out, not_33_out, not_34_out, not_35_out, not_36_out,
       not_37_out, not_38_out, not_39_out, not_40_out, not_41_out, not_42_out, not_43_out, not_44_out,
       not_45_out, not_46_out, not_47_out, not_48_out, not_49_out, not_50_out, not_51_out, not_52_out,
       not_53_out, not_54_out, not_55_out, not_56_out;

  not not_1 (not_1_out, A);
  and and_1 (and_1_out, not_1_out, not_2_out);
  not not_2 (not_2_out, B);
  not not_3 (not_3_out, A);
  and and_2 (and_2_out, not_3_out, not_4_out);
  not not_4 (not_4_out, C);
  not not_5 (not_5_out, A);
  and and_3 (and_3_out, not_5_out, not_6_out);
  not not_6 (not_6_out, D);
  not not_7 (not_7_out, B);
  and and_4 (and_4_out, not_7_out, not_8_out);
  not not_8 (not_8_out, D);
  not not_9 (not_9_out, A);
  and and_5 (and_5_out, not_9_out, not_10_out);
  not not_10 (not_10_out, B);
  not not_11 (not_11_out, A);
  and and_6 (and_6_out, not_11_out, not_12_out);
  not not_12 (not_12_out, D);
  not not_13 (not_13_out, B);
  and and_7 (and_7_out, not_13_out, not_14_out);
  not not_14 (not_14_out, D);
  not not_15 (not_15_out, A);
  and and_8 (and_8_out, not_15_out, C);
  not not_16 (not_16_out, B);
  and and_9 (and_9_out, not_16_out, C);
  not not_17 (not_17_out, A);
  and and_10 (and_10_out, not_17_out, not_18_out);
  not not_18 (not_18_out, C);
  not not_19 (not_19_out, B);
  not not_20 (not_20_out, C);
  and and_11 (and_11_out, not_19_out, not_20_out, not_21_out);
  not not_21 (not_21_out, D);
  not not_22 (not_22_out, B);
  and and_12 (and_12_out, not_22_out, C, D);
  not not_23 (not_23_out, A);
  and and_13 (and_13_out, not_23_out, B);
  not not_24 (not_24_out, A);
  and and_14 (and_14_out, not_24_out, not_25_out);
  not not_25 (not_25_out, B);
  not not_26 (not_26_out, B);
  and and_15 (and_15_out, not_26_out, not_27_out);
  not not_27 (not_27_out, D);
  not not_28 (not_28_out, A);
  and and_16 (and_16_out, not_28_out, not_29_out, D);
  not not_29 (not_29_out, C);
  not not_30 (not_30_out, A);
  and and_17 (and_17_out, not_30_out, C, not_31_out);
  not not_31 (not_31_out, D);
  not not_32 (not_32_out, B);
  not not_33 (not_33_out, D);
  not not_34 (not_34_out, A);
  not not_35 (not_35_out, B);
  not not_36 (not_36_out, A);
  not not_37 (not_37_out, D);
  not not_38 (not_38_out, A);
  not not_39 (not_39_out, C);
  not not_40 (not_40_out, B);
  not not_41 (not_41_out, C);
  not not_42 (not_42_out, D);
  not not_43 (not_43_out, B);
  not not_44 (not_44_out, A);
  not not_45 (not_45_out, C);
  not not_46 (not_46_out, A);
  not not_47 (not_47_out, D);
  not not_48 (not_48_out, A);
  and and_18 (and_18_out, not_48_out, not_49_out, D);
  not not_49 (not_49_out, C);
  not not_50 (not_50_out, B);
  and and_19 (and_19_out, not_50_out, D);
  not not_51 (not_51_out, B);
  and and_20 (and_20_out, not_51_out, C);
  not not_52 (not_52_out, A);
  not not_53 (not_53_out, B);
  not not_54 (not_54_out, D);
  not not_55 (not_55_out, A);
  not not_56 (not_56_out, C);
  or or_1 (a_2, and_1_out, and_2_out, and_3_out, and_4_out);
  or or_2 (b_2, and_5_out, and_6_out, and_7_out, and_8_out, and_9_out);
  or or_3 (c_2, and_10_out, and_11_out, and_12_out, and_13_out);
  or or_4 (d_2, and_14_out, and_15_out, and_16_out, and_17_out);
  and and_21 (and_21_out, not_32_out, not_33_out);
  and and_22 (and_22_out, not_34_out, not_35_out, C);
  and and_23 (and_23_out, not_36_out, C, not_37_out);
  and and_24 (and_24_out, not_38_out, B, not_39_out, D);
  and and_25 (and_25_out, not_40_out, not_41_out, not_42_out);
  and and_26 (and_26_out, not_43_out, C, D);
  and and_27 (and_27_out, not_44_out, B, not_45_out, D);
  and and_28 (and_28_out, not_46_out, B, C, not_47_out);
  or or_5 (g, and_18_out, and_19_out, and_20_out);
  and and_29 (and_29_out, not_52_out, not_53_out, C, not_54_out);
  or or_6 (ponto, and_29_out, and_30_out);
  and and_30 (and_30_out, not_55_out, B, not_56_out, D);
  or or_7 (e, and_21_out, and_22_out, and_23_out, and_24_out);
  or or_8 (f, and_25_out, and_26_out, and_27_out, and_28_out);
endmodule

module codificador_matricula (
  input  A,
  input  B,
  input  C,
  input  D,
  output a_2,
  output b_2,
  output c_2,
  output d_2,
  output e,
  output f,
  output g
);

  wire and_1_out, and_2_out, and_3_out, and_4_out, and_5_out, and_6_out, and_7_out, and_8_out, and_9_out,
       and_10_out, and_11_out, and_12_out, and_13_out, and_14_out, and_15_out, and_16_out, and_17_out,
       and_18_out, and_19_out, and_20_out, and_21_out, and_22_out, and_23_out, and_24_out, and_25_out,
       and_26_out, and_27_out, and_28_out, and_29_out, and_30_out, and_31_out, and_32_out, and_33_out,
       and_34_out, and_35_out, and_36_out, and_37_out, not_1_out, not_2_out, not_3_out, not_4_out, not_5_out,
       not_6_out, not_7_out, not_8_out, not_9_out, not_10_out, not_11_out, not_12_out, not_13_out,
       not_14_out, not_15_out, not_16_out, not_17_out, not_18_out, not_19_out, not_20_out, not_21_out,
       not_22_out, not_23_out, not_24_out, not_25_out, not_26_out, not_27_out, not_28_out, not_29_out,
       not_30_out, not_31_out, not_32_out, not_33_out, not_34_out, not_35_out, not_36_out, not_37_out,
       not_38_out, not_39_out, not_40_out, or_1_out, or_2_out, or_4_out, or_5_out, or_6_out, or_7_out,
       or_8_out, or_9_out;

  not not_1 (not_1_out, A);
  not not_2 (not_2_out, D);
  not not_3 (not_3_out, B);
  and and_1 (and_1_out, not_3_out, not_4_out);
  not not_4 (not_4_out, C);
  not not_5 (not_5_out, B);
  and and_2 (and_2_out, not_5_out, not_6_out);
  not not_6 (not_6_out, C);
  not not_7 (not_7_out, A);
  and and_3 (and_3_out, not_7_out, D);
  not not_8 (not_8_out, A);
  not not_9 (not_9_out, A);
  and and_4 (and_4_out, not_9_out, not_10_out);
  not not_10 (not_10_out, B);
  not not_11 (not_11_out, A);
  and and_5 (and_5_out, not_11_out, B);
  not not_12 (not_12_out, D);
  not not_13 (not_13_out, B);
  not not_14 (not_14_out, A);
  not not_15 (not_15_out, D);
  not not_16 (not_16_out, B);
  and and_6 (and_6_out, not_16_out, not_17_out);
  not not_17 (not_17_out, C);
  not not_18 (not_18_out, A);
  and and_7 (and_7_out, not_18_out, not_19_out);
  not not_19 (not_19_out, B);
  not not_20 (not_20_out, C);
  not not_21 (not_21_out, A);
  and and_8 (and_8_out, not_21_out, C);
  not not_22 (not_22_out, D);
  not not_23 (not_23_out, A);
  not not_24 (not_24_out, A);
  and and_9 (and_9_out, not_24_out, not_25_out);
  not not_25 (not_25_out, B);
  not not_26 (not_26_out, A);
  and and_10 (and_10_out, not_26_out, B);
  not not_27 (not_27_out, D);
  not not_28 (not_28_out, B);
  not not_29 (not_29_out, A);
  and and_11 (and_11_out, not_29_out, not_30_out);
  not not_30 (not_30_out, B);
  not not_31 (not_31_out, D);
  not not_32 (not_32_out, A);
  and and_12 (and_12_out, not_32_out, C);
  not not_33 (not_33_out, A);
  and and_13 (and_13_out, not_33_out, B);
  not not_34 (not_34_out, C);
  and and_14 (and_14_out, A, not_35_out);
  not not_35 (not_35_out, B);
  not not_36 (not_36_out, C);
  and and_15 (and_15_out, not_1_out, not_2_out);
  and and_16 (and_16_out, and_1_out, D);
  not not_37 (not_37_out, A);
  or or_1 (or_1_out, and_2_out, and_3_out);
  and and_17 (and_17_out, not_8_out, C);
  and and_18 (and_18_out, and_4_out, D);
  and and_19 (and_19_out, and_5_out, not_12_out);
  and and_20 (and_20_out, A, not_13_out);
  not not_38 (not_38_out, C);
  and and_21 (and_21_out, not_14_out, not_15_out);
  and and_22 (and_22_out, and_6_out, D);
  not not_39 (not_39_out, A);
  and and_23 (and_23_out, and_7_out, not_20_out);
  and and_24 (and_24_out, and_8_out, not_22_out);
  and and_25 (and_25_out, not_23_out, B);
  and and_26 (and_26_out, and_9_out, D);
  and and_27 (and_27_out, and_10_out, not_27_out);
  and and_28 (and_28_out, A, not_28_out);
  not not_40 (not_40_out, C);
  and and_29 (and_29_out, and_11_out, not_31_out);
  and and_30 (and_30_out, and_12_out, D);
  and and_31 (and_31_out, and_13_out, not_34_out);
  and and_32 (and_32_out, and_14_out, not_36_out);
  or or_2 (or_2_out, and_15_out, and_16_out);
  and and_33 (and_33_out, not_37_out, B);
  or or_3 (b_2, or_1_out, and_17_out);
  or or_4 (or_4_out, and_18_out, and_19_out);
  and and_34 (and_34_out, and_20_out, not_38_out);
  or or_5 (or_5_out, and_21_out, and_22_out);
  and and_35 (and_35_out, not_39_out, B);
  or or_6 (or_6_out, and_23_out, and_24_out);
  and and_36 (and_36_out, and_25_out, D);
  or or_7 (or_7_out, and_26_out, and_27_out);
  and and_37 (and_37_out, and_28_out, not_40_out);
  or or_8 (or_8_out, and_29_out, and_30_out);
  or or_9 (or_9_out, and_31_out, and_32_out);
  or or_10 (a_2, or_2_out, and_33_out);
  or or_11 (c_2, or_4_out, and_34_out);
  or or_12 (d_2, or_5_out, and_35_out);
  or or_13 (e, or_6_out, and_36_out);
  or or_14 (f, or_7_out, and_37_out);
  or or_15 (g, or_8_out, or_9_out);
endmodule
