// Logisim project maior_menor_igual.circ as structural Verilog: 1 circuit, main circuit main
module main (
  input  A___X1,
  input  B___X0,
  input  C___Y1,
  input  D___Y0,
  output out_5,
  output out_6,
  output X_Y
);

  wire and_1_out, and_2_out, and_3_out, and_4_out, and_5_out, and_7_out, xnor_1_out, xnor_2_out, xnor_3_out,
       xnor_4_out;

  and and_1 (and_1_out, A___X1, ~C___Y1);  // AND_Gate
  and and_2 (and_2_out, ~A___X1, C___Y1);  // AND_Gate
  and and_3 (and_3_out, B___X0, ~D___Y0);  // AND_Gate
  xnor xnor_1 (xnor_1_out, A___X1, C___Y1);
  xnor xnor_2 (xnor_2_out, A___X1, C___Y1);
  xnor xnor_3 (xnor_3_out, B___X0, D___Y0);
  and and_4 (and_4_out, ~B___X0, D___Y0);  // AND_Gate
  xnor xnor_4 (xnor_4_out, C___Y1, A___X1);
  and and_5 (and_5_out, and_3_out, xnor_1_out);
  and and_6 (out_6, xnor_2_out, xnor_3_out);
  and and_7 (and_7_out, and_4_out, xnor_4_out, xnor_4_out);
  or or_1 (out_5, and_5_out, and_1_out);
  or or_2 (X_Y, and_2_out, and_7_out);

  // Notes on the sheet:
  //   Nome: Gabriel Lorenson Schirmer
  //   Sistemas Digitais I
  //   Matrícula: 2024520249
  //   X>Y
  //   X=Y
endmodule
