// Logisim project media.circ as structural Verilog: 2 circuits, main circuit main
module teste_de_condicao (
  input  A,
  input  B,
  input  C,
  input  D,
  output [3:0] out_5,
  output [3:0] out_6
);

  wire and_1_out, and_2_out, not_1_out, or_1_out;

  and and_1 (and_1_out, A, C, D);
  and and_2 (and_2_out, A, B);
  or or_1 (or_1_out, and_1_out, and_2_out);
  Multiplexer #(.width(4), .enable("false")) multiplexer_1 (.in1(4'b1010), .out(out_5), .sel(or_1_out));  // open: in0
  Multiplexer #(.width(4), .enable("false")) multiplexer_2 (
    .in1({A, B, C, D}), .out(out_6), .sel(not_1_out));  // open: in0
  not not_1 (not_1_out, or_1_out);
endmodule

module main (
  input  [3:0] NOTA_1,
  input  [3:0] NOTA_2,
  input  [3:0] NOTA_DO_EXAME,
  output [4:0] out_4,
  output [5:0] out_5
);

  wire comparator_1_eq, comparator_1_gt, comparator_1_lt, comparator_2_eq, comparator_2_gt, comparator_2_lt,
       or_1_out, or_2_out;
  wire [3:0] teste_de_condicao_1_out_5, teste_de_condicao_2_out_5, teste_de_condicao_3_out_5;
  wire [4:0] adder_1_out, bit_extender_2_out, bit_extender_3_out, multiplexer_1_out;
  wire [5:0] adder_2_out, bit_extender_1_out, bit_extender_4_out, multiplier_1_out;

  teste_de_condicao teste_de_condicao_1 (
    .A(NOTA_1[3]), .B(NOTA_1[2]), .C(NOTA_1[1]), .D(NOTA_1[0]), .out_5(teste_de_condicao_1_out_5),
    .out_6(teste_de_condicao_1_out_5));
  teste_de_condicao teste_de_condicao_2 (
    .A(NOTA_2[3]), .B(NOTA_2[2]), .C(NOTA_2[1]), .D(NOTA_2[0]), .out_5(teste_de_condicao_2_out_5),
    .out_6(teste_de_condicao_2_out_5));
  Multiplexer #(.width(5)) multiplexer_1 (
    .in1(adder_1_out), .out(multiplexer_1_out), .sel(comparator_1_lt));  // open: in0, en
  assign bit_extender_1_out = {{2{1'b0}}, teste_de_condicao_3_out_5};  // Bit_Extender bit_extender_1
  teste_de_condicao teste_de_condicao_3 (
    .A(NOTA_DO_EXAME[3]), .B(NOTA_DO_EXAME[2]), .C(NOTA_DO_EXAME[1]), .D(NOTA_DO_EXAME[0]),
    .out_5(teste_de_condicao_3_out_5), .out_6(teste_de_condicao_3_out_5));
  assign bit_extender_2_out = {{1{1'b0}}, teste_de_condicao_1_out_5};  // Bit_Extender bit_extender_2
  assign bit_extender_3_out = {{1{1'b0}}, teste_de_condicao_2_out_5};  // Bit_Extender bit_extender_3
  assign bit_extender_4_out = {{1{1'b0}}, multiplexer_1_out};  // Bit_Extender bit_extender_4
  Multiplier #(.width(6)) multiplier_1 (
    .a(bit_extender_1_out), .b(6'b000010), .out(multiplier_1_out));  // open: cin, cout
  Adder #(.width(5)) adder_1 (.a(bit_extender_2_out), .b(bit_extender_3_out), .out(adder_1_out));  // open: cin, cout
  Adder #(.width(6)) adder_2 (.a(bit_extender_4_out), .b(multiplier_1_out), .out(adder_2_out));  // open: cin, cout
  Divider #(.width(5)) divider_1 (.a(adder_1_out), .b(5'b00010), .out(out_4));  // open: upper, rem
  or or_1 (or_1_out, comparator_1_gt, comparator_1_eq);
  LED led_1 (.in(or_1_out));
  Comparator #(.width(5), .mode("unsigned")) comparator_1 (
    .a(adder_1_out), .b(5'b01110), .gt(comparator_1_gt), .eq(comparator_1_eq), .lt(comparator_1_lt));
  Divider #(.width(6)) divider_2 (.a(adder_2_out), .b(6'b000100), .out(out_5));  // open: upper, rem
  Comparator #(.width(6), .mode("unsigned")) comparator_2 (
    .a(out_5), .b(6'b000101), .gt(comparator_2_gt), .eq(comparator_2_eq), .lt(comparator_2_lt));
  LED led_2 (.in(comparator_2_lt));
  LED led_3 (.in(or_2_out));
  or or_2 (or_2_out, comparator_2_gt, comparator_2_eq);

  // Notes on the sheet:
  //   NOTA_DO_EXAME: pull=down
  //   out_4: pull=down
  //   APROVADO
  //   MEDIA SEM EXAME
  //   APROVADO COM EXAME
  //   REPROVADO
  //   MEDIA COM EXAME
endmodule
