// Logisim project primo.circ as structural Verilog: 1 circuit, main circuit main
module main (
  input  [3:0] in_1,
  output out_2
);

  wire and_1_out, and_2_out, and_3_out, and_4_out, and_5_out, or_1_out, xor_1_out;

  and and_1 (and_1_out, ~in_1[2], in_1[1]);  // AND_Gate
  and and_2 (and_2_out, in_1[2], in_1[0]);
  or or_1 (or_1_out, and_1_out, and_2_out);
  xor xor_1 (xor_1_out, in_1[2], in_1[1]);
  and and_3 (and_3_out, in_1[0], in_1[3]);
  and and_4 (and_4_out, ~in_1[3], or_1_out);  // AND_Gate
  and and_5 (and_5_out, xor_1_out, and_3_out);
  or or_2 (out_2, and_4_out, and_5_out);

  // Notes on the sheet:
  //   Matrícula: 2024520249
  //   Sistemas Digitais I
  //   Nome: Gabriel Lorenson Schirmer
  //   Liga se o número é primo (4 bits)
  //   Números possíveis
  //   0010 = 2
  //   0011 = 3 
  //   0101 = 5
  //   0111 = 7
  //   1011 = 11
  //   1101 = 13
endmodule
